// Logisim project lab13.circ as structural Verilog: 2 circuits, main circuit sum
module sum (
  input  p_prev,
  input  a,
  input  b,
  output s,
  output p_next
);

  wire and_1_out, and_2_out, xor_1_out;

  xor xor_1 (xor_1_out, a, b);
  and and_1 (and_1_out, b, a);
  xor xor_2 (s, p_prev, xor_1_out);
  and and_2 (and_2_out, xor_1_out, p_prev);
  or or_1 (p_next, and_2_out, and_1_out);
endmodule

module main_0 (
  input  a,
  input  in_2,
  input  in_3,
  input  in_4,
  input  b,
  input  in_6,
  input  in_7,
  input  in_8
);

  wire sum_1_p_next, sum_1_s, sum_2_p_next, sum_2_s, sum_3_p_next, sum_3_s, sum_4_p_next, sum_4_s;

  // Probe on sum_3_s
  LED p (.in(sum_4_p_next));
  // Probe on sum_4_s
  sum sum_1 (.p_prev(1'b0), .a(in_8), .b(in_4), .s(sum_1_s), .p_next(sum_1_p_next));
  sum sum_2 (.p_prev(sum_1_p_next), .a(in_7), .b(in_3), .s(sum_2_s), .p_next(sum_2_p_next));
  sum sum_3 (.p_prev(sum_2_p_next), .a(in_2), .b(in_6), .s(sum_3_s), .p_next(sum_3_p_next));
  sum sum_4 (.p_prev(sum_3_p_next), .a(a), .b(b), .s(sum_4_s), .p_next(sum_4_p_next));
  // Probe on sum_2_s
  // Probe on sum_1_s

  // Notes on the sheet:
  //   s
endmodule
