// Logisim project lab14.circ as structural Verilog: 2 circuits, main circuit static_ram
module static_ram (
  input  D1,
  input  WR,
  input  Y,
  input  X,
  output D0
);

  wire and_1_out, and_2_out, and_3_out, d_ff_1_q, not_1_out;

  and and_1 (and_1_out, Y, X);
  and and_2 (and_2_out, WR, and_1_out);
  D_Flip_Flop d_ff_1 (.clk(and_2_out), .D(D1), .Q(d_ff_1_q));  // open: Qn, preset, en, reset
  not not_1 (not_1_out, WR);
  assign D0 = and_3_out ? d_ff_1_q : 1'bz;  // Controlled_Buffer controlled_buffer_1
  and and_3 (and_3_out, not_1_out, and_1_out);
endmodule

module main (
  input  WR_RD,
  input  in_2,
  input  in_3,
  input  in_4,
  input  in_5
);

  wire static_ram_1_d0, static_ram_2_d0, static_ram_3_d0, static_ram_4_d0;

  static_ram static_ram_1 (.D1(in_2), .WR(WR_RD), .Y(1'b1), .X(1'b1), .D0(static_ram_1_d0));
  static_ram static_ram_2 (.D1(in_3), .WR(WR_RD), .Y(1'b1), .X(1'b1), .D0(static_ram_2_d0));
  static_ram static_ram_3 (.D1(in_4), .WR(WR_RD), .Y(1'b1), .X(1'b1), .D0(static_ram_3_d0));
  static_ram static_ram_4 (.D1(in_5), .WR(WR_RD), .Y(1'b1), .X(1'b1), .D0(static_ram_4_d0));
  LED led_1 (.in(static_ram_1_d0));
  LED led_2 (.in(static_ram_2_d0));
  LED led_3 (.in(static_ram_4_d0));
  LED led_4 (.in(static_ram_3_d0));
endmodule
