// Logisim project lab15.circ as structural Verilog: 2 circuits, main circuit main
module main (
  input  A0,
  input  A1,
  input  RD,
  input  CS
);

  wire not_1_out, not_2_out, not_3_out, not_4_out, rom_1_y, rom_2_y, rom_3_y, rom_4_y, rom_5_y, rom_6_y,
       rom_7_y, rom_8_y;

  not not_1 (not_1_out, A0);
  not not_2 (not_2_out, A1);
  not not_3 (not_3_out, RD);
  not not_4 (not_4_out, CS);
  LED D0 (.in(rom_1_y));
  rom rom_1 (.A0(not_1_out), .A1(not_2_out), .RD(not_3_out), .CS(not_4_out), .Y(rom_1_y));
  LED D1 (.in(rom_2_y));
  rom rom_2 (.A0(not_1_out), .A1(not_2_out), .RD(not_3_out), .CS(not_4_out), .Y(rom_2_y));
  LED D2 (.in(rom_3_y));
  rom rom_3 (.A0(not_1_out), .A1(not_2_out), .RD(not_3_out), .CS(not_4_out), .Y(rom_3_y));
  LED D3 (.in(rom_4_y));
  rom rom_4 (.A0(not_1_out), .A1(not_2_out), .RD(not_3_out), .CS(not_4_out), .Y(rom_4_y));
  rom rom_5 (.A0(not_1_out), .A1(not_2_out), .RD(not_3_out), .CS(not_4_out), .Y(rom_5_y));
  LED D4 (.in(rom_5_y));
  rom rom_6 (.A0(not_1_out), .A1(not_2_out), .RD(not_3_out), .CS(not_4_out), .Y(rom_6_y));
  LED D5 (.in(rom_6_y));
  LED D6 (.in(rom_7_y));
  rom rom_7 (.A0(not_1_out), .A1(not_2_out), .RD(not_3_out), .CS(not_4_out), .Y(rom_7_y));
  LED D7 (.in(rom_8_y));
  rom rom_8 (.A0(not_1_out), .A1(not_2_out), .RD(not_3_out), .CS(not_4_out), .Y(rom_8_y));
endmodule

module rom (
  input  A0,
  input  A1,
  input  RD,
  input  CS,
  output Y
);

  wire [2:2] and_1_out;

  Multiplexer #(.select(3), .enable("false")) multiplexer_1 (
    .in0(1'b0), .in1(1'b1), .in2(1'b1), .in3(1'b1), .in4(1'b0), .in5(1'b0), .in6(1'b1), .in7(1'b0), .out(Y),
    .sel({and_1_out[2], A1, A0}));
  and and_1 (and_1_out[2], RD, CS);
endmodule
