// Logisim project lab15_ROM.circ as structural Verilog: 4 circuits, main circuit main
module main (
  input  A0,
  input  A1,
  input  A2,
  input  RD,
  input  CS
);

  wire not_1_out, not_2_out, not_3_out, not_4_out, not_5_out, romupd_1_y, romupd_2_y, romupd_3_y, romupd_4_y;

  not not_1 (not_1_out, A0);
  not not_2 (not_2_out, A1);
  not not_3 (not_3_out, A2);
  not not_4 (not_4_out, RD);
  not not_5 (not_5_out, CS);
  ROMUPD romupd_1 (
    .A2(not_1_out), .A1(not_2_out), .A0(not_3_out), .RD(not_4_out), .CS(not_5_out), .Y(romupd_1_y));  // open: Not_Y
  LED led_1 (.in(romupd_1_y));
  ROMUPD romupd_2 (
    .A2(not_1_out), .A1(not_2_out), .A0(not_3_out), .RD(not_4_out), .CS(not_5_out), .Y(romupd_2_y));  // open: Not_Y
  LED led_2 (.in(romupd_2_y));
  ROMUPD romupd_3 (
    .A2(not_1_out), .A1(not_2_out), .A0(not_3_out), .RD(not_4_out), .CS(not_5_out), .Y(romupd_3_y));  // open: Not_Y
  LED led_3 (.in(romupd_3_y));
  ROMUPD romupd_4 (
    .A2(not_1_out), .A1(not_2_out), .A0(not_3_out), .RD(not_4_out), .CS(not_5_out), .Y(romupd_4_y));  // open: Not_Y
  LED led_4 (.in(romupd_4_y));
endmodule

module ROM (
  input  A0,
  input  A1,
  input  A2,
  input  RD,
  input  CS,
  output Y
);

  wire and_1_out;

  and and_1 (and_1_out, RD, CS);
  Multiplexer #(.select(3)) multiplexer_1 (
    .in0(1'b0), .in1(1'b1), .in2(1'b1), .in3(1'b1), .in4(1'b0), .in5(1'b0), .in6(1'b1), .in7(1'b0), .out(Y),
    .en(A0));  // open: sel
endmodule

module MS (
  input  X0,
  input  X1,
  input  X2,
  input  X3,
  input  X4,
  input  X5,
  input  X6,
  input  X7,
  input  E,
  input  A2,
  input  A1,
  input  A0,
  output Not_Y,
  output Y
);

  wire nor_1_out, nor_2_out, not_1_out, not_2_out, not_3_out, not_4_out, or_1_out, or_2_out, or_3_out,
       or_4_out, or_5_out, or_6_out, or_7_out, or_8_out;

  nor nor_1 (nor_1_out, E, A2);
  not not_1 (not_1_out, A1);
  not not_2 (not_2_out, A0);
  nor nor_2 (nor_2_out, E, nor_1_out);
  not not_3 (not_3_out, not_1_out);
  not not_4 (not_4_out, not_2_out);
  or or_1 (or_1_out, X0, nor_1_out, not_1_out, not_2_out);
  or or_2 (or_2_out, X1, nor_1_out, not_1_out, not_4_out);
  or or_3 (or_3_out, X2, nor_1_out, not_3_out, not_2_out);
  or or_4 (or_4_out, X3, nor_1_out, not_3_out, not_4_out);
  or or_5 (or_5_out, X4, nor_2_out, not_1_out, not_2_out);
  or or_6 (or_6_out, X5, nor_2_out, not_1_out, not_4_out);
  or or_7 (or_7_out, X6, nor_2_out, not_3_out, not_2_out);
  or or_8 (or_8_out, X7, nor_2_out, not_3_out, not_4_out);
  and and_1 (Y, or_1_out, or_2_out, or_3_out, or_4_out, or_5_out, or_6_out, or_7_out, or_8_out);
  not not_5 (Not_Y, Y);
endmodule

module ROMUPD (
  input  A2,
  input  A1,
  input  A0,
  input  RD,
  input  CS,
  output Not_Y,
  output Y
);

  wire and_1_out;

  and and_1 (and_1_out, RD, CS);
  MS ms_1 (
    .X0(1'b0), .X1(1'b1), .X2(1'b1), .X3(1'b1), .X4(1'b0), .X5(1'b0), .X6(1'b1), .X7(1'b0), .E(and_1_out),
    .A2(A2), .A1(A1), .A0(A0), .Not_Y(Not_Y), .Y(Y));
endmodule
